// Logisim project ALU.circ as structural Verilog: 1 circuit, main circuit ALU
module ALU (
  input  [31:0] A,
  input  [31:0] B,
  input  [4:0] Shift,
  input  CarryIn,
  input  [3:0] Codop,
  output [31:0] S,
  output [3:0] Flags
);

  wire [31:0] adder_1_out, adder_2_out, adder_3_out, ANDD_out, BIC_out, EOR_out, multiplexer_1_out,
       multiplier_1_out, not_1_out, not_2_out, ORR_out, shifter_1_out, shifter_2_out, shifter_3_out,
       shifter_4_out, subtractor_1_out, subtractor_2_out, subtractor_3_out, subtractor_4_out, TST_out;

  assign ANDD_out = A & B;  // AND_Gate ANDD, 32 bits wide
  assign EOR_out = A ^ B;  // XOR_Gate EOR, 32 bits wide
  Shifter #(.width(32)) shifter_1 (.in(B), .\dist (Shift), .out(shifter_1_out));
  Shifter #(.width(32), .shift("lr")) shifter_2 (.in(B), .\dist (Shift), .out(shifter_2_out));
  Shifter #(.width(32), .shift("ar")) shifter_3 (.in(B), .\dist (Shift), .out(shifter_3_out));
  Adder #(.width(32)) adder_1 (.a(A), .b(B), .out(adder_1_out), .cin(CarryIn));  // open: cout
  Subtractor #(.width(32)) subtractor_1 (.a(A), .b(B), .out(subtractor_1_out));  // open: bin, bout
  Subtractor #(.width(32)) subtractor_2 (
    .a({32{1'b0}}), .b(32'h1), .out(subtractor_2_out), .bin(CarryIn));  // open: bout
  Shifter #(.width(32), .shift("rr")) shifter_4 (.in(B), .\dist (Shift), .out(shifter_4_out));
  assign TST_out = A & B;  // AND_Gate TST, 32 bits wide
  Subtractor #(.width(32)) subtractor_3 (.a({32{1'b0}}), .b(B), .out(subtractor_3_out));  // open: bin, bout
  Subtractor #(.width(32)) subtractor_4 (.a(A), .b(B), .out(subtractor_4_out));  // open: bin, bout
  Adder #(.width(32)) adder_2 (.a(A), .b(B), .out(adder_2_out));  // open: cin, cout
  assign ORR_out = A | B;  // OR_Gate ORR, 32 bits wide
  Multiplier #(.width(32)) multiplier_1 (.a(A), .b(B), .out(multiplier_1_out));  // open: cin, cout
  assign not_1_out = ~B;  // NOT_Gate not_1, 32 bits wide
  assign not_2_out = ~B;  // NOT_Gate not_2, 32 bits wide
  Adder #(.width(32)) adder_3 (.a(subtractor_1_out), .b(subtractor_2_out), .out(adder_3_out));  // open: cin, cout
  assign BIC_out = A & not_1_out;  // AND_Gate BIC, 32 bits wide
  Multiplexer #(.select(4), .width(32), .enable("false")) multiplexer_1 (
    .in0(ANDD_out), .in1(EOR_out), .in2(shifter_1_out), .in3(shifter_2_out), .in4(shifter_3_out),
    .in5(adder_1_out), .in6(adder_3_out), .in7(shifter_4_out), .in8(TST_out), .in9(subtractor_3_out),
    .in10(subtractor_4_out), .in11(adder_2_out), .in12(ORR_out), .in13(multiplier_1_out), .in14(BIC_out),
    .in15(not_2_out), .out(multiplexer_1_out));  // open: sel
  Comparator #(.width(32)) comparator_1 (
    .a(multiplexer_1_out), .b({32{1'b0}}), .eq(Flags[1]), .lt(Flags[0]));  // open: gt
  Multiplexer #(.select(4), .width(32), .enable("false")) multiplexer_2 (
    .in0(ANDD_out), .in1(EOR_out), .in2(shifter_1_out), .in3(shifter_2_out), .in4(shifter_3_out),
    .in5(adder_1_out), .in6(adder_3_out), .in7(shifter_4_out), .in8(TST_out), .in9(subtractor_3_out),
    .in10(subtractor_4_out), .in11(adder_2_out), .in12(ORR_out), .in13(multiplier_1_out), .in14(BIC_out),
    .in15(not_2_out), .out(S));  // open: sel

  // Other names for the same wires on the sheet: N = Flags[0]; Z = Flags[1]; C = Flags[2]; V = Flags[3]

  // Notes on the sheet:
  //   Note: for ROR, C = N
  //   Note 2: assume that shift > 0 for LSL and LSR
endmodule
