// Logisim project Controller.circ as structural Verilog: 13 circuits, main circuit Controller
module Controller (
  input  [15:0] Inst,
  input  [3:0] Flags,
  input  Clk,
  input  Reset,
  output Carry,
  output DP_Shift,
  output Imm32_Enable,
  output [4:0] Imm5,
  output [31:0] Imm32,
  output [3:0] ALU_Opcode,
  output [2:0] Rm,
  output [2:0] Rn,
  output [2:0] Rd,
  output [31:0] RAM_Addr,
  output Load,
  output Store,
  output [7:0] PC
);

  wire conditional_final_1_verified, load_store_final_1_pc_hold, not_1_out, Opcode_Decoder_1_conditional,
       Opcode_Decoder_1_data_processing, Opcode_Decoder_1_load_store, Opcode_Decoder_1_shift,
       Opcode_Decoder_1_sp_address, Shift_Add_Sub_Mov_1_carry, SP_Address_1_write_enable;
  wire [2:0] data_processing_final_1_rd, data_processing_final_1_rm, data_processing_final_1_rn,
       load_store_final_1_rd, load_store_final_1_rm, Shift_Add_Sub_Mov_1_rd, Shift_Add_Sub_Mov_1_rm,
       Shift_Add_Sub_Mov_1_rn;
  wire [3:0] data_processing_final_1_alu_opcode, data_processing_final_1_flags_update_mask,
       flags_apsr_1_flags_out, or_1_out, Shift_Add_Sub_Mov_1_alu_opcode,
       Shift_Add_Sub_Mov_1_flags_update_mask;
  wire [7:0] adder_1_out, adder_2_out, conditional_final_1_offset;
  wire [31:0] SP_Address_1_new_stack_pointer, Stack_Pointer_q;

  Register #(.width(32)) Stack_Pointer (
    .D(SP_Address_1_new_stack_pointer), .en(SP_Address_1_write_enable), .clk(Clk), .Q(Stack_Pointer_q),
    .clr(Reset));
  Opcode_Decoder_FINAL Opcode_Decoder_1 (
    .Opcode(Inst[15:10]), .Shift(Opcode_Decoder_1_shift), .Data_Processing(Opcode_Decoder_1_data_processing),
    .Load_Store(Opcode_Decoder_1_load_store), .SP_Address(Opcode_Decoder_1_sp_address),
    .Conditional(Opcode_Decoder_1_conditional));
  assign or_1_out = data_processing_final_1_flags_update_mask | Shift_Add_Sub_Mov_1_flags_update_mask;  // OR_Gate or_1, 4 bits wide
  Shift_Add_Sub_Mov_FINAL Shift_Add_Sub_Mov_1 (
    .Instruction(Inst), .Enable(Opcode_Decoder_1_shift), .Carry(Shift_Add_Sub_Mov_1_carry),
    .Imm32_Enable(Imm32_Enable), .Imm5(Imm5), .Imm32(Imm32), .ALU_Opcode(Shift_Add_Sub_Mov_1_alu_opcode),
    .Rm(Shift_Add_Sub_Mov_1_rm), .Rn(Shift_Add_Sub_Mov_1_rn), .Rd(Shift_Add_Sub_Mov_1_rd),
    .Flags_Update_Mask(Shift_Add_Sub_Mov_1_flags_update_mask));
  Data_Processing_FINAL data_processing_final_1 (
    .Enable(Opcode_Decoder_1_data_processing), .Instruction(Inst),
    .Flags_Update_Mask(data_processing_final_1_flags_update_mask),
    .ALU_Opcode(data_processing_final_1_alu_opcode), .Rm(data_processing_final_1_rm),
    .Rd(data_processing_final_1_rd), .Rn(data_processing_final_1_rn));
  Flags_APSR flags_apsr_1 (
    .Flags_In(or_1_out), .Update_Mask(Flags), .Clk(Clk), .Rst(Reset), .Flags_Out(flags_apsr_1_flags_out));
  Load_Store_FINAL load_store_final_1 (
    .Enable(Opcode_Decoder_1_load_store), .Instruction(Inst), .Clk(Clk), .Reset(Reset),
    .Stack_Pointer(Stack_Pointer_q), .Store(Load), .Load(Store), .PC_Hold(load_store_final_1_pc_hold),
    .RAM_Addr(RAM_Addr), .Rm(load_store_final_1_rm), .Rd(load_store_final_1_rd));
  SP_Address_FINAL SP_Address_1 (
    .New_Stack_Pointer(SP_Address_1_new_stack_pointer), .Stack_Pointer(Stack_Pointer_q),
    .Enable(Opcode_Decoder_1_sp_address), .Instruction(Inst), .Write_Enable(SP_Address_1_write_enable));
  Conditional_FINAL conditional_final_1 (
    .Enable(Opcode_Decoder_1_conditional), .Instruction(Inst), .N(flags_apsr_1_flags_out[3]),
    .Z(flags_apsr_1_flags_out[2]), .C(flags_apsr_1_flags_out[1]), .V(flags_apsr_1_flags_out[0]),
    .Offset(conditional_final_1_offset), .Verified(conditional_final_1_verified));
  Adder adder_1 (.a(8'h3), .b(conditional_final_1_offset), .out(adder_1_out), .cin(1'b0));  // open: cout
  Adder adder_2 (.a(adder_1_out), .b(PC), .out(adder_2_out), .cin(1'b0));  // open: cout
  and and_1 (DP_Shift, Opcode_Decoder_1_shift, ~Opcode_Decoder_1_data_processing);  // AND_Gate
  not not_1 (not_1_out, load_store_final_1_pc_hold);
  Counter counter_1 (
    .clr(Reset), .load(conditional_final_1_verified), .up(1'b1), .count(not_1_out), .clk(Clk),
    .D(adder_2_out), .Q(PC));  // open: carry
  Multiplexer #(.enable("false")) multiplexer_1 (
    .in0(flags_apsr_1_flags_out[1]), .in1(Shift_Add_Sub_Mov_1_carry), .out(Carry), .sel(DP_Shift));
  assign ALU_Opcode = Shift_Add_Sub_Mov_1_alu_opcode | data_processing_final_1_alu_opcode;  // OR_Gate or_2, 4 bits wide
  assign Rm = Shift_Add_Sub_Mov_1_rm | data_processing_final_1_rm | load_store_final_1_rm;  // OR_Gate or_3, 3 bits wide
  assign Rn = Shift_Add_Sub_Mov_1_rn | data_processing_final_1_rn;  // OR_Gate or_4, 3 bits wide
  assign Rd = Shift_Add_Sub_Mov_1_rd | data_processing_final_1_rd | load_store_final_1_rd;  // OR_Gate or_5, 3 bits wide

  // Notes on the sheet:
  //   Extract carry
  //   Extract Opcode
  //   IF Reg_Imm=1 THEN use shift value from register ELSE use shift value from Imm5
  //   Buffer flags for next instruction
  //   Add 3 to offset because ARM pre-increments PC
  //   and does an additionnal prefect operation
endmodule

module Conditional_FINAL (
  input  Enable,
  input  [15:0] Instruction,
  input  N,
  input  Z,
  input  C,
  input  V,
  output [7:0] Offset,
  output Verified
);

  wire and_1_out, and_2_out, and_3_out, Cequal0, Cequal1, comparator_5_eq, comparator_5_gt, comparator_5_lt,
       multiplexer_1_out, Nequal0, Nequal1, or_1_out, or_2_out, or_3_out, Vequal0, Vequal1, Zequal0, Zequal1;

  Comparator #(.width(1)) comparator_1 (.a(N), .b(1'b1), .gt(Nequal0), .eq(Nequal1));  // open: lt
  Comparator #(.width(1)) comparator_2 (.a(Z), .b(1'b1), .gt(Zequal0), .eq(Zequal1));  // open: lt
  Comparator #(.width(1)) comparator_3 (.a(C), .b(1'b1), .gt(Cequal0), .eq(Cequal1));  // open: lt
  Comparator #(.width(1)) comparator_4 (.a(V), .b(1'b1), .gt(Vequal0), .eq(Vequal1));  // open: lt
  Comparator #(.width(1)) comparator_5 (.a(N), .b(V), .gt(comparator_5_gt), .eq(comparator_5_eq), .lt(comparator_5_lt));
  and and_1 (and_1_out, Cequal1, Zequal0);
  or or_1 (or_1_out, Cequal0, Zequal1);
  or or_2 (or_2_out, comparator_5_gt, comparator_5_lt);
  and and_2 (and_2_out, comparator_5_eq, Zequal0);
  or or_3 (or_3_out, or_2_out, Zequal1);
  Multiplexer #(.select(4), .enable("false")) multiplexer_1 (
    .in0(Zequal1), .in1(Zequal0), .in2(Cequal1), .in3(Cequal0), .in4(Nequal1), .in5(Nequal0), .in6(Vequal1),
    .in7(Vequal0), .in8(and_1_out), .in9(or_1_out), .in10(comparator_5_eq), .in11(or_2_out),
    .in12(and_2_out), .in13(or_3_out), .in14(1'b1), .out(multiplexer_1_out), .sel(Instruction[11:8]));  // open: in15
  Multiplexer #(.width(8), .enable("false")) multiplexer_2 (
    .in0({8{1'b0}}), .in1(Instruction[7:0]), .out(Offset), .sel(and_3_out));
  and and_3 (and_3_out, multiplexer_1_out, Enable);
  Multiplexer #(.enable("false")) multiplexer_3 (.in0(1'b0), .in1(multiplexer_1_out), .out(Verified), .sel(Enable));

  // Other names for the same wires on the sheet: Offset_t[7:0] = Instruction[7:0]; Condition[3:0] = Instruction[11:8]
endmodule

module Load_Store_FINAL (
  input  Enable,
  input  [15:0] Instruction,
  input  Clk,
  input  Reset,
  input  [31:0] Stack_Pointer,
  output Store,
  output Load,
  output PC_Hold,
  output [31:0] RAM_Addr,
  output [2:0] Rm,
  output [2:0] Rd
);

  wire and_1_out, d_ff_1_q, not_1_out, or_1_out;
  wire [31:0] adder_1_out;

  Adder #(.width(32)) adder_1 (
    .a(Stack_Pointer), .b({{24{1'b0}}, Instruction[7:0]}), .out(adder_1_out));  // open: cin, cout
  and and_1 (and_1_out, or_1_out, ~d_ff_1_q);  // AND_Gate
  not not_1 (not_1_out, Instruction[11]);
  or or_1 (or_1_out, Instruction[11], not_1_out);
  D_Flip_Flop d_ff_1 (.D(and_1_out), .clk(Clk), .Q(d_ff_1_q), .reset(Reset));  // open: Qn, preset
  Multiplexer #(.enable("false")) multiplexer_1 (.in0(1'b0), .in1(not_1_out), .out(Store), .sel(Enable));
  Multiplexer #(.enable("false")) multiplexer_2 (.in0(1'b0), .in1(Instruction[11]), .out(Load), .sel(Enable));
  Multiplexer #(.enable("false")) multiplexer_3 (.in0(1'b0), .in1(d_ff_1_q), .out(PC_Hold), .sel(Enable));
  Multiplexer #(.width(32), .enable("false")) multiplexer_4 (
    .in0({32{1'b0}}), .in1(adder_1_out), .out(RAM_Addr), .sel(Enable));
  Multiplexer #(.width(3), .enable("false")) multiplexer_5 (
    .in0(3'b000), .in1(Instruction[10:8]), .out(Rd), .sel(Enable));

  assign Rm = Rd;

  // Other names for the same wires on the sheet: imm8[7:0] = Instruction[7:0]; Rt[2:0] = Instruction[10:8]
endmodule

module Data_Processing_FINAL (
  input  Enable,
  input  [15:0] Instruction,
  output [3:0] Flags_Update_Mask,
  output [3:0] ALU_Opcode,
  output [2:0] Rm,
  output [2:0] Rd,
  output [2:0] Rn
);

  wire [2:0] rd_out, rm_out, rn_out;
  wire [3:0] flags_update_dp_1_v;

  Multiplexer #(.select(4), .width(3), .enable("false")) multiplexer_1 (
    .in0(Instruction[5:3]), .in1(Instruction[5:3]), .in2(Instruction[5:3]), .in3(Instruction[5:3]),
    .in4(Instruction[5:3]), .in5(Instruction[5:3]), .in6(Instruction[5:3]), .in7(Instruction[5:3]),
    .in8(Instruction[5:3]), .in9(Instruction[5:3]), .in10(Instruction[5:3]), .in11(Instruction[5:3]),
    .in12(Instruction[5:3]), .in13(Instruction[5:3]), .in14(Instruction[5:3]), .in15(Instruction[5:3]),
    .out(rm_out), .sel(Instruction[9:6]));
  Multiplexer #(.select(4), .width(3), .enable("false")) multiplexer_2 (
    .in0(Instruction[2:0]), .in1(Instruction[2:0]), .in2(Instruction[2:0]), .in3(Instruction[2:0]),
    .in4(Instruction[2:0]), .in5(Instruction[2:0]), .in6(Instruction[2:0]), .in7(Instruction[2:0]),
    .in8(Instruction[2:0]), .in9(Instruction[2:0]), .in10(Instruction[2:0]), .in11(Instruction[2:0]),
    .in12(Instruction[2:0]), .in13(Instruction[2:0]), .in14(Instruction[2:0]), .in15(Instruction[2:0]),
    .out(rd_out), .sel(Instruction[9:6]));
  flags_update_DP flags_update_dp_1 (
    .opcode_3(Instruction[9]), .opcode_2(Instruction[8]), .opcode_1(Instruction[7]),
    .opcode_0(Instruction[6]), .N(flags_update_dp_1_v[3]), .Z(flags_update_dp_1_v[2]),
    .C(flags_update_dp_1_v[1]), .V(flags_update_dp_1_v[0]));
  Multiplexer #(.select(4), .width(3), .enable("false")) multiplexer_3 (
    .in0(Instruction[2:0]), .in1(Instruction[2:0]), .in2(Instruction[2:0]), .in3(Instruction[2:0]),
    .in4(Instruction[2:0]), .in5(Instruction[2:0]), .in6(Instruction[2:0]), .in7(Instruction[2:0]),
    .in8(3'b000), .in9(Instruction[2:0]), .in10(3'b000), .in11(3'b000), .in12(Instruction[2:0]),
    .in13(Instruction[2:0]), .in14(Instruction[2:0]), .in15(3'b000), .out(rn_out), .sel(Instruction[9:6]));
  Multiplexer #(.width(4), .enable("false")) multiplexer_4 (
    .in0(4'b0000), .in1(flags_update_dp_1_v), .out(Flags_Update_Mask), .sel(Enable));
  Multiplexer #(.width(4), .enable("false")) multiplexer_5 (
    .in0(4'b0000), .in1(Instruction[9:6]), .out(ALU_Opcode), .sel(Enable));
  Multiplexer #(.width(3), .enable("false")) multiplexer_6 (.in0(3'b000), .in1(rm_out), .out(Rm), .sel(Enable));
  Multiplexer #(.width(3), .enable("false")) multiplexer_7 (.in0(3'b000), .in1(rd_out), .out(Rd), .sel(Enable));
  Multiplexer #(.width(3), .enable("false")) multiplexer_8 (.in0(3'b000), .in1(rn_out), .out(Rn), .sel(Enable));

  // Other names for the same wires on the sheet: FourFiveSix[2:0] = Instruction[5:3];
  //   OneTwoThree[2:0] = Instruction[2:0]

  // Notes on the sheet:
  //   Pull output low on Enable = 0
  //   Note 2: RSB instruction has Rn as 1st operand.
  //   Pull output low on Enable = 0
  //   MUL instruction has Rn as 1st operand and Rdm as 2nd operand
  //   For simplification purposes, Rm is used for 1st operand both here and in the ALU.
  //   Note: instructions that does not save the result will still have the second operand as the destination register, the ALU will copy the second register to the destination register
endmodule

module Opcode_Decoder_FINAL (
  input  [5:0] Opcode,
  output Shift,
  output Data_Processing,
  output Load_Store,
  output SP_Address,
  output Conditional
);

  wire not_1_out, not_2_out, not_3_out;

  not not_1 (not_1_out, Opcode[5]);
  not not_2 (not_2_out, Opcode[4]);
  not not_3 (not_3_out, Opcode[3]);
  and and_1 (Shift, not_1_out, not_2_out);
  and and_2 (Data_Processing, not_1_out, Opcode[4]);
  and and_3 (Load_Store, Opcode[5], not_2_out, not_3_out);
  and and_4 (SP_Address, Opcode[5], not_2_out, Opcode[3]);
  and and_5 (Conditional, Opcode[5], Opcode[4]);

  // Other names for the same wires on the sheet: e10 = Opcode[0]; e11 = Opcode[1]; e12 = Opcode[2]; e13 = Opcode[3];
  //   e14 = Opcode[4]; e15 = Opcode[5]

  // Notes on the sheet:
  //   Shift, add, sub, mov
  //   Load/Store
  //   SP Address
  //   Conditional branch
  //   Data Processing
endmodule

module Shift_Add_Sub_Mov_FINAL (
  input  [15:0] Instruction,
  input  Enable,
  output Carry,
  output Imm32_Enable,
  output [4:0] Imm5,
  output [31:0] Imm32,
  output [3:0] ALU_Opcode,
  output [2:0] Rm,
  output [2:0] Rn,
  output [2:0] Rd,
  output [3:0] Flags_Update_Mask
);

  wire and_1_out, and_2_out, not_1_out, opcode_intern_decoder_1_s_add_sub, opcode_intern_decoder_1_s_mov,
       opcode_intern_decoder_1_s_shift, s_Carry, s_Imm32_Enable;
  wire [2:0] imm32_add_sub, or_2_out, or_3_out, Rd_add_sub, Rd_mov, Rd_shift, Rm_add_sub, Rn_add_sub,
       Rn_shift;
  wire [3:0] s_ALU_Opcode, s_Flags_Update_Mask;
  wire [4:0] s_Imm5;
  wire [7:0] imm32_mov;
  wire [31:0] or_1_out;

  opcode_SASM opcode_sasm_1 (
    .e_9(Instruction[9]), .e_10(Instruction[10]), .e_11(Instruction[11]), .e_12(Instruction[12]),
    .e_13(Instruction[13]), .s_4(s_ALU_Opcode[3]), .s_3(s_ALU_Opcode[2]), .s_2(s_ALU_Opcode[1]),
    .s_1(s_ALU_Opcode[0]));
  not not_1 (not_1_out, Instruction[10]);
  assign or_1_out = {{29{1'b0}}, imm32_add_sub} | {{24{1'b0}}, imm32_mov};  // OR_Gate or_1, 32 bits wide
  opcode_intern_decoder opcode_intern_decoder_1 (
    .e_4(s_ALU_Opcode[3]), .e_3(s_ALU_Opcode[2]), .e_2(s_ALU_Opcode[1]), .e_1(s_ALU_Opcode[0]),
    .s_SHIFT(opcode_intern_decoder_1_s_shift), .s_ADD_SUB(opcode_intern_decoder_1_s_add_sub),
    .s_MOV(opcode_intern_decoder_1_s_mov));
  assign or_2_out = Rn_shift | Rn_add_sub;  // OR_Gate or_2, 3 bits wide
  assign or_3_out = Rd_mov | Rd_shift | Rd_add_sub;  // OR_Gate or_3, 3 bits wide
  and and_1 (and_1_out, opcode_intern_decoder_1_s_add_sub, Instruction[10]);
  and and_2 (and_2_out, opcode_intern_decoder_1_s_add_sub, not_1_out);
  Multiplexer #(.width(4), .enable("false")) multiplexer_1 (
    .in0(4'b0000), .in1(s_Flags_Update_Mask), .out(Flags_Update_Mask), .sel(Enable));
  Multiplexer #(.enable("false")) multiplexer_2 (.in0(1'b0), .in1(s_Carry), .out(Carry), .sel(Enable));
  Multiplexer #(.enable("false")) multiplexer_3 (.in0(1'b0), .in1(s_Imm32_Enable), .out(Imm32_Enable), .sel(Enable));
  Multiplexer #(.width(4), .enable("false")) multiplexer_4 (
    .in0(4'b0000), .in1(s_ALU_Opcode), .out(ALU_Opcode), .sel(Enable));
  Multiplexer #(.width(3), .enable("false")) multiplexer_5 (.in0(3'b000), .in1(Rm_add_sub), .out(Rm), .sel(Enable));
  Multiplexer #(.width(3), .enable("false")) multiplexer_6 (.in0(3'b000), .in1(or_2_out), .out(Rn), .sel(Enable));
  Multiplexer #(.width(3), .enable("false")) multiplexer_7 (.in0(3'b000), .in1(or_3_out), .out(Rd), .sel(Enable));
  Multiplexer #(.width(5), .enable("false")) multiplexer_8 (.in0({5{1'b0}}), .in1(s_Imm5), .out(Imm5), .sel(Enable));
  Multiplexer #(.width(32), .enable("false")) multiplexer_9 (
    .in0({32{1'b0}}), .in1(or_1_out), .out(Imm32), .sel(Enable));
  Multiplexer #(.width(5), .enable("false")) multiplexer_10 (
    .in0({5{1'b0}}), .in1(Instruction[10:6]), .out(s_Imm5), .sel(opcode_intern_decoder_1_s_shift));
  Multiplexer #(.width(3), .enable("false")) multiplexer_11 (
    .in0(3'b000), .in1(Instruction[5:3]), .out(Rn_shift), .sel(opcode_intern_decoder_1_s_shift));
  Multiplexer #(.width(3), .enable("false")) multiplexer_12 (
    .in0(3'b000), .in1(Instruction[2:0]), .out(Rd_shift), .sel(opcode_intern_decoder_1_s_shift));
  Multiplexer #(.width(3), .enable("false")) multiplexer_13 (
    .in0(3'b000), .in1(Instruction[8:6]), .out(imm32_add_sub), .sel(and_1_out));
  Multiplexer #(.width(3), .enable("false")) multiplexer_14 (
    .in0(3'b000), .in1(Instruction[8:6]), .out(Rm_add_sub), .sel(and_2_out));
  Multiplexer #(.width(3), .enable("false")) multiplexer_15 (
    .in0(3'b000), .in1(Instruction[5:3]), .out(Rn_add_sub), .sel(opcode_intern_decoder_1_s_add_sub));
  Multiplexer #(.width(3), .enable("false")) multiplexer_16 (
    .in0(3'b000), .in1(Instruction[2:0]), .out(Rd_add_sub), .sel(opcode_intern_decoder_1_s_add_sub));
  Multiplexer #(.width(3), .enable("false")) multiplexer_17 (
    .in0(3'b000), .in1(Instruction[10:8]), .out(Rd_mov), .sel(opcode_intern_decoder_1_s_mov));
  Multiplexer #(.width(8), .enable("false")) multiplexer_18 (
    .in0({8{1'b0}}), .in1(Instruction[7:0]), .out(imm32_mov), .sel(opcode_intern_decoder_1_s_mov));
  carry_SASM carry_sasm_1 (
    .e4(s_ALU_Opcode[3]), .e3(s_ALU_Opcode[2]), .e2(s_ALU_Opcode[1]), .e1(s_ALU_Opcode[0]), .out_5(s_Carry));
  flags_SASM flags_sasm_1 (
    .e4(s_ALU_Opcode[3]), .e3(s_ALU_Opcode[2]), .e2(s_ALU_Opcode[1]), .e1(s_ALU_Opcode[0]),
    .N(s_Flags_Update_Mask[3]), .Z(s_Flags_Update_Mask[2]), .C(s_Flags_Update_Mask[1]),
    .V(s_Flags_Update_Mask[0]));
  or or_4 (s_Imm32_Enable, and_1_out, opcode_intern_decoder_1_s_mov);

  // Other names for the same wires on the sheet: e6 = Instruction[6]; e7 = Instruction[7]; e8 = Instruction[8];
  //   e9 = Instruction[9]; e10 = Instruction[10]; e3 = Instruction[3]; e4 = Instruction[4]; e5 = Instruction[5];
  //   e0 = Instruction[0]; e1 = Instruction[1]; e2 = Instruction[2]; e_enable = Enable; e11 = Instruction[11];
  //   e12 = Instruction[12]; e13 = Instruction[13]; e14 = Instruction[14]; e15 = Instruction[15];
  //   out_alu_opcode[3:0] = ALU_Opcode; out_carry = Carry; out_flags_update_mask[3:0] = Flags_Update_Mask;
  //   out_imm5[4:0] = Imm5; out_imm32[31:0] = Imm32; out_imm32_enable = Imm32_Enable; out_rd[2:0] = Rd;
  //   out_rm[2:0] = Rm; out_rn[2:0] = Rn

  // Notes on the sheet:
  //   Pull output low on Enable = 0
  //   Note 3: Imm32_Enable forces the use of the immediate for Rm register
  //   Note: ALU uses Rn register for shifts. Use Rn instead of Rm for shifts (immediate) here too
  //   Note 2: MOV uses RSB ALU opcode with Imm8 reversed so that it is copied to output register
  //   imm5 - shift
  //   Rn - shift
  //   Rd - shift
  //   OK
  //   OK
  //   OK
  //   OK
  //   OK
  //   OK
  //   OK
  //   OK
  //   OK
  //   imm3 - add/sub
  //   Rm - add/sub
  //   Rn - add/sub
  //   Rd - add/sub
  //   Rd - mov
  //   imm8 - mov
  //   Ordre NZCV
  //   ALU will use Imm32 instead of Rm
  //   Enable carry for SUB since it is reversed in ALU
  //   imm32 - add/sub
  //   imm32 - mov
endmodule

module SP_Address_FINAL (
  input  Enable,
  input  [15:0] Instruction,
  input  [31:0] Stack_Pointer,
  output Write_Enable,
  output [31:0] New_Stack_Pointer
);

  wire and_1_out, not_1_out;
  wire [31:0] adder_1_out, s_new_stack_pointer, subtractor_1_out;

  not not_1 (not_1_out, Instruction[14]);
  and and_1 (and_1_out, Instruction[12], Instruction[13], not_1_out, Instruction[15]);
  Subtractor #(.width(32)) subtractor_1 (
    .a(Stack_Pointer), .b({{25{1'b0}}, Instruction[6:0]}), .out(subtractor_1_out));  // open: bin, bout
  Adder #(.width(32)) adder_1 (
    .a(Stack_Pointer), .b({{25{1'b0}}, Instruction[6:0]}), .out(adder_1_out));  // open: cin, cout
  Multiplexer #(.width(32), .enable("false")) multiplexer_1 (
    .in0(adder_1_out), .in1(subtractor_1_out), .out(s_new_stack_pointer), .sel(Instruction[7]));
  Multiplexer #(.enable("false")) multiplexer_2 (.in0(1'b0), .in1(and_1_out), .out(Write_Enable), .sel(Enable));
  Multiplexer #(.width(32), .enable("false")) multiplexer_3 (
    .in0({32{1'b0}}), .in1(s_new_stack_pointer), .out(New_Stack_Pointer), .sel(Enable));

  // Other names for the same wires on the sheet: e_enable = Enable

  // Notes on the sheet:
  //   Pull output low on Enable = 0
endmodule

module Flags_APSR (
  input  [3:0] Flags_In,
  input  [3:0] Update_Mask,
  input  Clk,
  input  Rst,
  output [3:0] Flags_Out
);

  Register #(.width(1)) register_1 (.D(Flags_In[0]), .en(Update_Mask[0]), .clk(Clk), .Q(Flags_Out[0]), .clr(Rst));
  Register #(.width(1)) register_2 (.D(Flags_In[1]), .en(Update_Mask[1]), .clk(Clk), .Q(Flags_Out[1]), .clr(Rst));
  Register #(.width(1)) register_3 (.D(Flags_In[2]), .en(Update_Mask[2]), .clk(Clk), .Q(Flags_Out[2]), .clr(Rst));
  Register #(.width(1)) register_4 (.D(Flags_In[3]), .en(Update_Mask[3]), .clk(Clk), .Q(Flags_Out[3]), .clr(Rst));

  // Other names for the same wires on the sheet: Reset = Rst
endmodule

module opcode_SASM (
  input  e_9,
  input  e_10,
  input  e_11,
  input  e_12,
  input  e_13,
  output s_4,
  output s_3,
  output s_2,
  output s_1
);

  wire and_1_out, and_2_out, and_3_out, and_4_out, not_1_out, not_2_out, not_3_out, not_4_out;

  not not_1 (not_1_out, e_12);
  not not_2 (not_2_out, e_13);
  not not_3 (not_3_out, e_9);
  not not_4 (not_4_out, e_12);
  and and_1 (and_1_out, not_1_out, not_2_out);
  and and_2 (and_2_out, e_9, e_11);
  and and_3 (and_3_out, not_3_out, e_11);
  and and_4 (and_4_out, e_11, not_4_out);
  or or_1 (s_2, and_1_out, and_2_out);
  or or_2 (s_1, e_13, and_3_out, and_4_out);

  assign s_3 = e_12;
  assign s_4 = e_13;
endmodule

module opcode_intern_decoder (
  input  e_4,
  input  e_3,
  input  e_2,
  input  e_1,
  output s_SHIFT,
  output s_ADD_SUB,
  output s_MOV
);

  wire and_1_out, and_2_out, and_3_out, and_4_out, not_1_out, not_2_out, not_3_out, not_4_out, not_5_out,
       not_6_out, not_7_out, not_8_out, not_9_out, not_10_out, not_11_out;

  not not_1 (not_1_out, e_4);
  not not_2 (not_2_out, e_3);
  not not_3 (not_3_out, e_4);
  not not_4 (not_4_out, e_2);
  not not_5 (not_5_out, e_1);
  not not_6 (not_6_out, e_4);
  not not_7 (not_7_out, e_2);
  not not_8 (not_8_out, e_4);
  not not_9 (not_9_out, e_1);
  not not_10 (not_10_out, e_3);
  not not_11 (not_11_out, e_2);
  and and_1 (and_1_out, not_1_out, not_2_out, e_2);
  and and_2 (and_2_out, not_3_out, e_3, not_4_out, not_5_out);
  and and_3 (and_3_out, not_6_out, e_3, not_7_out, e_1);
  and and_4 (and_4_out, not_8_out, e_3, e_2, not_9_out);
  and and_5 (s_MOV, e_4, not_10_out, not_11_out, e_1);
  or or_1 (s_SHIFT, and_1_out, and_2_out);
  or or_2 (s_ADD_SUB, and_3_out, and_4_out);
endmodule

module flags_SASM (
  input  e4,
  input  e3,
  input  e2,
  input  e1,
  output N,
  output Z,
  output C,
  output V
);

  wire and_1_out, and_2_out, and_3_out, and_4_out, and_5_out, and_6_out, and_7_out, and_8_out, and_9_out,
       and_10_out, and_11_out, and_12_out, and_13_out, not_1_out, not_2_out, not_3_out, not_4_out, not_5_out,
       not_6_out, not_7_out, not_8_out, not_9_out, not_10_out, not_11_out, not_12_out, not_13_out,
       not_14_out, not_15_out, not_16_out, not_17_out, not_18_out, not_19_out, not_20_out, not_21_out,
       not_22_out, not_23_out, not_24_out, not_25_out, not_26_out;

  not not_1 (not_1_out, e4);
  not not_2 (not_2_out, e3);
  not not_3 (not_3_out, e4);
  not not_4 (not_4_out, e2);
  not not_5 (not_5_out, e4);
  not not_6 (not_6_out, e1);
  not not_7 (not_7_out, e3);
  not not_8 (not_8_out, e2);
  not not_9 (not_9_out, e4);
  not not_10 (not_10_out, e3);
  not not_11 (not_11_out, e4);
  not not_12 (not_12_out, e2);
  not not_13 (not_13_out, e4);
  not not_14 (not_14_out, e1);
  not not_15 (not_15_out, e3);
  not not_16 (not_16_out, e2);
  not not_17 (not_17_out, e4);
  not not_18 (not_18_out, e3);
  not not_19 (not_19_out, e4);
  not not_20 (not_20_out, e2);
  not not_21 (not_21_out, e4);
  not not_22 (not_22_out, e1);
  not not_23 (not_23_out, e4);
  not not_24 (not_24_out, e2);
  not not_25 (not_25_out, e4);
  not not_26 (not_26_out, e1);
  and and_1 (and_1_out, not_1_out, not_2_out, e2);
  and and_2 (and_2_out, not_3_out, e3, not_4_out);
  and and_3 (and_3_out, not_5_out, e3, not_6_out);
  and and_4 (and_4_out, e4, not_7_out, not_8_out, e1);
  and and_5 (and_5_out, not_9_out, not_10_out, e2);
  and and_6 (and_6_out, not_11_out, e3, not_12_out);
  and and_7 (and_7_out, not_13_out, e3, not_14_out);
  and and_8 (and_8_out, e4, not_15_out, not_16_out, e1);
  and and_9 (and_9_out, not_17_out, not_18_out, e2);
  and and_10 (and_10_out, not_19_out, e3, not_20_out);
  and and_11 (and_11_out, not_21_out, e3, not_22_out);
  and and_12 (and_12_out, not_23_out, e3, not_24_out, e1);
  and and_13 (and_13_out, not_25_out, e3, e2, not_26_out);
  or or_1 (N, and_1_out, and_2_out, and_3_out, and_4_out);
  or or_2 (Z, and_5_out, and_6_out, and_7_out, and_8_out);
  or or_3 (C, and_9_out, and_10_out, and_11_out);
  or or_4 (V, and_12_out, and_13_out);
endmodule

module carry_SASM (
  input  e4,
  input  e3,
  input  e2,
  input  e1,
  output out_5
);

  wire not_1_out, not_2_out;

  not not_1 (not_1_out, e4);
  not not_2 (not_2_out, e1);
  and and_1 (out_5, not_1_out, e3, e2, not_2_out);
endmodule

module flags_update_DP (
  input  opcode_3,
  input  opcode_2,
  input  opcode_1,
  input  opcode_0,
  output N,
  output Z,
  output C,
  output V
);

  wire and_1_out, and_2_out, and_3_out, and_4_out, not_1_out, not_2_out, not_3_out, not_4_out, not_5_out,
       not_6_out, not_7_out, not_8_out, not_9_out;

  not not_1 (not_1_out, opcode_3);
  not not_2 (not_2_out, opcode_2);
  not not_3 (not_3_out, opcode_0);
  not not_4 (not_4_out, opcode_3);
  not not_5 (not_5_out, opcode_1);
  not not_6 (not_6_out, opcode_3);
  not not_7 (not_7_out, opcode_0);
  not not_8 (not_8_out, opcode_2);
  not not_9 (not_9_out, opcode_2);
  or or_1 (C, not_1_out, not_2_out, not_3_out, opcode_1);
  and and_1 (and_1_out, not_4_out, opcode_2, not_5_out, opcode_0);
  and and_2 (and_2_out, not_6_out, opcode_2, opcode_1, not_7_out);
  and and_3 (and_3_out, opcode_3, not_8_out, opcode_0);
  and and_4 (and_4_out, opcode_3, not_9_out, opcode_1);
  or or_2 (V, and_1_out, and_2_out, and_3_out, and_4_out);

  assign N = 1'b1;
  assign Z = 1'b1;
endmodule
